# Fritzing sketch fadingFritz (saved by Fritzing 0.9.3b)
circuit board: 6.88566cm x 5.36311cm
breadboards: 2

parts:
  R4 = Resistor [resistance=220 tolerance=±5% package=THT]
  LED2 = LED - 5mm [color="Red (633nm)" package="5 mm [THT]"]
  R3 = Rotary Potentiometer (Small) [maximum_resistance=100kΩ package=THT]
  Arduino2 = Arduino Uno (Rev3)
  S2 = Pushbutton [package=THT]
  R5 = Resistor [tolerance=±5% resistance=10k package=THT]
  S3 = Pushbutton [package=THT]
  R6 = Resistor [tolerance=±5% resistance=10k package=THT]

nets (from the breadboard view):
  N1: R4.Pin_0, LED2.anode
  N2: R4.Pin_1, Arduino2.D9_PWM
  N3: LED2.cathode, R3.leg2, Arduino2.GND, R5.Pin_1, R6.Pin_1
  N4: R3.leg1, Arduino2.5V, S2.leg1, S3.leg1
  N5: R3.wiper, Arduino2.A0
  N6: Arduino2.D2, S2.leg0
  N7: Arduino2.D4, S3.leg0, R6.Pin_0

notes:
  In this example, potentiometer values are read in through an 'Analog In' pin. The values are then used to control the modulation of an LED on a PWM pin. Related examples: http://arduino.cc/en/Tutorial/AnalogInput http://arduino.cc/en/Tutorial/Fading
